// Logisim project 200_Register_Parallel-Load.circ as structural Verilog: 4 circuits, main circuit main
module main (
  input  in_1,
  input  in_2,
  input  in_3,
  input  [1:0] in_4,
  input  in_5,
  output out_6,
  output out_7,
  output [1:0] out_8
);

  wire clock_1_out, clock_2_out, n2x1_mux_1_d, n2x1_mux_2_d;

  Clock clock_1 (.out(clock_1_out));
  Clock clock_2 (.out(clock_2_out));
  _2x1_MUX u_2x1_mux_1 (.i0(out_6), .i1(in_1), .d(n2x1_mux_1_d), .s(in_3));
  _2x1_MUX u_2x1_mux_2 (.i0(out_7), .i1(in_2), .d(n2x1_mux_2_d), .s(in_3));
  D_Flip_Flop d_ff_1 (.clk(clock_1_out), .D(n2x1_mux_1_d), .Q(out_6));  // open: Qn, preset, en, reset
  _2_bit_Parallel_Load_Reg u_2_bit_parallel_load_reg_1 (
    .load(in_5), .clk(clock_2_out), .i1(in_4[1]), .i0(in_4[0]), .q1(out_8[1]), .q0(out_8[0]));
  D_Flip_Flop d_ff_2 (.clk(clock_1_out), .D(n2x1_mux_2_d), .Q(out_7));  // open: Qn, preset, en, reset

  // Notes on the sheet:
  //   2-bit Parallel-Load Register
endmodule

module _2x1_MUX (
  input  i0,
  input  i1,
  input  s,
  output d
);

  wire and_1_out, and_2_out, not_1_out;

  not not_1 (not_1_out, s);
  and and_1 (and_1_out, i0, not_1_out);
  and and_2 (and_2_out, i1, s);
  or or_1 (d, and_1_out, and_2_out);

  // Notes on the sheet:
  //   d=[i0 * (s0)'] + [i1 * s0]
endmodule

module _4x1_MUX (
  input  i0,
  input  i1,
  input  i2,
  input  i3,
  input  s1,
  input  s0,
  output d
);

  wire and_1_out, and_2_out, and_3_out, and_4_out, not_1_out, not_2_out;

  not not_1 (not_1_out, s1);
  and and_1 (and_1_out, i0, not_1_out, not_2_out);
  and and_2 (and_2_out, i1, not_1_out, s0);
  and and_3 (and_3_out, i2, s1, not_2_out);
  and and_4 (and_4_out, i3, s1, s0);
  not not_2 (not_2_out, s0);
  or or_1 (d, and_1_out, and_2_out, and_3_out, and_4_out);
endmodule

module _2_bit_Parallel_Load_Reg (
  input  i1,
  input  i0,
  input  load,
  input  clk,
  output q1,
  output q0
);

  wire n2x1_mux_1_d, n2x1_mux_2_d;

  _2x1_MUX u_2x1_mux_1 (.i0(q1), .i1(i1), .d(n2x1_mux_1_d), .s(load));
  _2x1_MUX u_2x1_mux_2 (.i0(q0), .i1(i0), .d(n2x1_mux_2_d), .s(load));
  D_Flip_Flop d_ff_1 (.clk(clk), .D(n2x1_mux_1_d), .Q(q1));  // open: Qn, preset, en, reset
  D_Flip_Flop d_ff_2 (.clk(clk), .D(n2x1_mux_2_d), .Q(q0));  // open: Qn, preset, en, reset

  // Notes on the sheet:
  //   2-bit Parallel-Load Register
endmodule
